# Fritzing sketch hackfest2015 (saved by Fritzing 0.9.2b)
perfboards: 20

parts:
  rp01 = Raspberry Pi 2
  ar01 = Arduino Mega 2560 (Rev3)
  casino_(lcd01) = 128 x 64 Graphic LCD
  LED2 = smd LED [color="Red (633nm)" package="0805 [SMD]"]
  R2 = Resistor [tolerance=±5% resistance=330 package=THT]
  ar02a = Arduino Uno (Rev3) - ICSP
  ar02b = Rotoshield - Motor driver shield for Arduino
  J1 = shrouded pin header, 10 pins [form="♂ (shrouded male)"]  # not connected
  R3 = Photocell (LDR) [package=THT]
  R4 = Resistor [tolerance=±5% resistance=10k package="2512 [SMD]"]
  R1 = Resistor [tolerance=±5% resistance=10k package=THT]
  5v = Power plug
  LED3 = LED - 3mm [color="Red (633nm)" package="3 mm [THT]"]  # not connected
  LED4 = LED - 3mm [color="Red (633nm)" package="3 mm [THT]"]  # not connected
  LED5 = LED - 3mm [color="Red (633nm)" package="3 mm [THT]"]  # not connected
  LED6 = LED - 3mm [color="Red (633nm)" package="3 mm [THT]"]  # not connected
  LED7 = LED - 3mm [color="Red (633nm)" package="3 mm [THT]"]  # not connected
  fluidmotor01_(12v) = Plastic Solenoid Valve
  solenoid01_(12v) = Plastic Solenoid Valve
  flowmeter01 = Plastic Solenoid Valve
  U1 = LCD-16X2 [package=lcd-16x2]
  R6 = Resistor [tolerance=±5% resistance=220 package=THT]  # not connected
  X1 = USB Connectors [package=usb-a-s]  # not connected
  12v = Power plug
  5v_2 = Power plug
  U2 = SN74LS21N [package="DIP14 [THT]"]  # not connected
  U3 = SN74LS20N [package="DIP14 [THT]"]
  U5 = G3VM-61E1 [package=g3vm-61e1]
  U6 = G3VM-61E1 [package=g3vm-61e1]
  U7 = G3VM-61E1 [package=g3vm-61e1]
  U8 = G3VM-61E1 [package=g3vm-61e1]
  ar03 = Arduino Uno (Rev3) - ICSP
  R7 = Trimmer Potentiometer [maximum_resistance=10kΩ package=THT]
  U9 = G3VM-61E1 [package=g3vm-61e1]
  U10 = G3VM-61E1 [package=g3vm-61e1]

nets:
  GND: rp01.GND, ar01.GND, ar02a.GND, ar02b.GND, 5v.GND, flowmeter01.no_name_yet#2, U1.VSS, U1.R_W, U3.1C, ar03.GND, R7.leg2
  N1: ar01.D2_PWM, casino_(lcd01).4_D/I
  N2: ar01.D3_PWM, casino_(lcd01).3_Vo
  N3: ar01.D4_PWM, U9.P$2, U10.P$2
  N4: ar01.D22, casino_(lcd01).6_Enable
  N5: ar01.D23, casino_(lcd01).5_R/W
  N6: ar01.D29, R2.Pin_1
  N7: casino_(lcd01).1_Vss, casino_(lcd01).15_CS1, casino_(lcd01).20_K(-), R4.Pin_0, 5v_2.GND
  N8: casino_(lcd01).2_Vdd, R3.pin_1, R1.Pin_1, 5v_2.VCC
  N9: LED2.anode, R2.Pin_0
  N10: ar02a.A0, R3.pin_0, R4.Pin_1
  VCC: ar02b.VCC, 5v.VCC, flowmeter01.no_name_yet#1, U1.VDD
  N11: fluidmotor01_(12v).no_name_yet#1, 12v.VCC, U5.P$6, U6.P$4
  N12: fluidmotor01_(12v).no_name_yet#2, 12v.GND, U5.P$4
  N13: solenoid01_(12v).no_name_yet#1, U8.P$6
  N14: U1.RS, ar03.D7
  N15: U1.E, ar03.D8
  N16: U1.DB4, ar03.D9_PWM
  N17: U1.DB5, ar03.D10_PWM/SS
  N18: U1.DB6, ar03.D11_PWM/MOSI
  N19: U1.DB7, ar03.D12/MISO
  N20: U5.P$2, ar03.D2
  N21: U6.P$6, U7.P$4
  N22: U7.P$6, U8.P$4
